# Fritzing sketch DHT22_Sketch (saved by Fritzing 0.9.0b)
perfboards: 1

parts:
  RHT1 = Humidity and Temperature Sensor RHT03
  Part1 = Triple Axis Accelerometer Breakout - ADXL345  # not connected
  R1 = Resistor [tolerance=±10% resistance=10k package=THT]
  RHT2 = Humidity and Temperature Sensor RHT03  # not connected
  R2 = Resistor [tolerance=±10% resistance=10k package=THT]  # not connected
  JP3 = Header 3 [package=1x03-1mm-ra]  # not connected
  JP4 = Header 3 [package=1x03-1mm-ra]

nets:
  N1: RHT1.Vcc, JP4.2
  N2: RHT1.Data-signal, R1.Pin_0
  N3: RHT1.GND_2, JP4.1
